// Logisim project M60的BCD码计数器.circ as structural Verilog: 2 circuits, main circuit main
module main (
  input  in_1,
  input  in_2,
  output out_3,
  output out_4,
  output out_5,
  output out_6,
  output out_7,
  output out_8
);

  wire _2_q0, _2_q2, \n74161计数器_1_q0 , \n74161计数器_1_q3 , nand_2_out, not_1_out;

  nand nand_1 (in_1, \n74161计数器_1_q3 , _2_q2, _2_q0, \n74161计数器_1_q0 );
  \_74161计数器  _2 (
    .\LD非 (in_1), .D0(1'b0), .D1(1'b0), .D2(1'b0), .D3(1'b0), .CTp(not_1_out), .CTt(not_1_out), .Q1(out_3),
    .Q2(_2_q2), .Q3(out_4), .CO(out_5), .\CR非 (1'b1), .CP(in_2), .Q0(_2_q0));
  nand nand_2 (nand_2_out, \n74161计数器_1_q3 , \n74161计数器_1_q0 );
  not not_1 (not_1_out, nand_2_out);
  \_74161计数器  \u_74161计数器_1  (
    .\LD非 (nand_2_out), .D0(1'b0), .D1(1'b0), .D2(1'b0), .D3(1'b0), .CTp(1'b1), .CTt(1'b1), .Q1(out_6),
    .Q2(out_7), .Q3(\n74161计数器_1_q3 ), .CO(out_8), .\CR非 (1'b1), .CP(in_2), .Q0(\n74161计数器_1_q0 ));

  // Notes on the sheet:
  //   （1）
endmodule

module \_74161计数器  (
  input  \LD非 ,
  input  D0,
  input  D1,
  input  CP,
  input  D2,
  input  D3,
  input  \CR非 ,
  input  CTp,
  input  CTt,
  output Q0,
  output Q1,
  output Q2,
  output Q3,
  output CO
);

  wire and_1_out, and_2_out, and_3_out, and_4_out, and_5_out, and_6_out, and_7_out, and_8_out, and_9_out,
       and_10_out, and_11_out, and_12_out, nand_1_out, nand_2_out, nand_3_out, nand_4_out, nand_5_out,
       nand_6_out, nand_7_out, nand_8_out, not_1_out, not_2_out, not_3_out, or_1_out, or_2_out, or_3_out,
       or_4_out;

  not not_1 (not_1_out, \LD非 );
  not not_2 (not_2_out, CP);
  not not_3 (not_3_out, \CR非 );
  and and_1 (and_1_out, CTp, CTt);
  and and_2 (and_2_out, Q0, and_1_out);
  and and_3 (and_3_out, Q1, Q0, and_1_out);
  and and_4 (and_4_out, Q2, Q1, Q0, and_1_out);
  nand nand_1 (nand_1_out, not_1_out, nand_2_out);
  nand nand_2 (nand_2_out, D0, not_1_out);
  nand nand_3 (nand_3_out, not_1_out, nand_4_out);
  nand nand_4 (nand_4_out, D1, not_1_out);
  nand nand_5 (nand_5_out, not_1_out, nand_6_out);
  nand nand_6 (nand_6_out, D2, not_1_out);
  nand nand_7 (nand_7_out, not_1_out, nand_8_out);
  nand nand_8 (nand_8_out, D3, not_1_out);
  or or_1 (or_1_out, and_1_out, not_1_out);
  or or_2 (or_2_out, and_2_out, not_1_out);
  or or_3 (or_3_out, and_3_out, not_1_out);
  or or_4 (or_4_out, and_4_out, not_1_out);
  and and_5 (and_5_out, nand_1_out, or_1_out);
  and and_6 (and_6_out, or_1_out, nand_2_out);
  and and_7 (and_7_out, nand_3_out, or_2_out);
  and and_8 (and_8_out, or_2_out, nand_4_out);
  and and_9 (and_9_out, nand_5_out, or_3_out);
  and and_10 (and_10_out, or_3_out, nand_6_out);
  and and_11 (and_11_out, nand_7_out, or_4_out);
  and and_12 (and_12_out, or_4_out, nand_8_out);
  J_K_Flip_Flop j_k_ff_1 (
    .J(and_5_out), .clk(not_2_out), .K(and_6_out), .Q(Q0), .reset(not_3_out));  // open: Qn, preset, en
  J_K_Flip_Flop j_k_ff_2 (
    .J(and_7_out), .clk(not_2_out), .K(and_8_out), .Q(Q1), .reset(not_3_out));  // open: Qn, preset, en
  J_K_Flip_Flop j_k_ff_3 (
    .J(and_9_out), .clk(not_2_out), .K(and_10_out), .Q(Q2), .reset(not_3_out));  // open: Qn, preset, en
  J_K_Flip_Flop j_k_ff_4 (
    .J(and_11_out), .clk(not_2_out), .K(and_12_out), .Q(Q3), .reset(not_3_out));  // open: Qn, preset, en
  and and_13 (CO, Q3, Q2, Q1, Q0, CTt);
endmodule
