// Logisim project M60的BCD码计数器1.circ as structural Verilog: 1 circuit, main circuit main
module main (
  output \进位 ,
  output out_2,
  output \个位_低四位BCD ,
  output out_4,
  output out_5,
  output out_6,
  output \十位_高四位BCD ,
  output out_8,
  output out_9
);

  wire _1_co, _2_co, clock_1_out, nand_1_out, nand_2_out, not_1_out;

  \_74161计数器  _2 (
    .\LD非 (1'b1), .D0(1'b0), .D1(1'b0), .D2(1'b0), .D3(1'b0), .CTp(1'b1), .CTt(1'b1), .Q1(\十位_高四位BCD ),
    .Q2(out_8), .Q3(out_9), .CO(_2_co), .\CR非 (nand_1_out), .CP(not_1_out), .Q0(out_6));
  not not_1 (not_1_out, nand_2_out);
  and and_1 (\进位 , out_6, out_8, out_2, out_5);
  nand nand_1 (nand_1_out, out_8, \十位_高四位BCD );
  \_74161计数器  _1 (
    .\LD非 (1'b1), .D0(1'b0), .D1(1'b0), .D2(1'b0), .D3(1'b0), .CTp(1'b1), .CTt(1'b1), .Q1(\个位_低四位BCD ),
    .Q2(out_4), .Q3(out_5), .CO(_1_co), .\CR非 (nand_2_out), .CP(clock_1_out), .Q0(out_2));
  Clock clock_1 (.out(clock_1_out));
  nand nand_2 (nand_2_out, \个位_低四位BCD , out_5);

  // Notes on the sheet:
  //   模6
  //   模10
endmodule
